# Fritzing sketch power_control_1 (saved by Fritzing 0.9.4)
breadboards: 1

parts:
  R4 = Resistor [tolerance=±5% resistance=10k package=THT]
  Q2 = NPN-Transistor [part_number=2N4401 package="TO92 [THT]"]
  Q1 = Basic FET P-Channel [part_number=NDP6020P package="TO220 [THT]"]
  R6 = Resistor [tolerance=±5% resistance=100k package=THT]

nets:
  N1: R4.Pin_1, Q2.B
  GND: Q2.E
  N2: Q2.C, Q1.gate, R6.Pin_1
  3.3V: Q1.source, R6.Pin_0
