# Fritzing sketch prototype_5.28.20 (saved by Fritzing 0.9.4)
breadboards: 1

parts:
  Part1 = Arduino Pro Mini (3.3V)
  LED3 = LED - 3mm [color="Red (633nm)" package="3 mm [THT]"]
  R1 = Resistor [tolerance=±5% resistance=1k package=THT]
  V1 = DC Power [voltage=3.3V]

nets:
  N1: Part1.VCC, V1.V+
  GND: Part1.GND, V1.V-
  N2: Part1.D9, LED3.anode
  N3: LED3.cathode, R1.Pin_0
